# Fritzing sketch ATTiny84-Remote (saved by Fritzing 0.8.7b)
circuit board: 8cm x 6cm
breadboards: 1

parts:
  Attiny84 = ATTiny84 [chip_label=ATTiny84 package="DIP (Dual Inline) [THT]"]
  S1 = Pushbutton [package="[THT]"]
  S2 = Pushbutton [package="[THT]"]
  S3 = Pushbutton [package="[THT]"]
  S4 = Pushbutton [package="[THT]"]
  LED1 = LED - 5mm [color="Red (633nm)" package="5 mm [THT]"]
  LED2 = LED - 5mm [color="Red (633nm)" package="5 mm [THT]"]
  S5 = Pushbutton [package="[THT]"]
  R3 = Resistor [tolerance=±5% resistance=10k package=THT]
  R4 = Resistor [tolerance=±5% resistance=10k package=THT]
  R5 = Resistor [tolerance=±5% resistance=10k package=THT]
  R7 = Resistor [tolerance=±5% resistance=220 package=THT]
  S6 = Pushbutton [package=THT]
  R2 = Resistor [tolerance=±5% resistance=10k package=THT]
  R1 = Resistor [tolerance=±5% resistance=10k package=THT]
  J1 = female pin header, 4 pins [form="♀ (female)"]
  S7 = Pushbutton [package="[THT]"]
  R8 = Resistor [tolerance=±5% resistance=10k package=THT]
  R6 = Resistor [tolerance=±5% resistance=220 package=THT]
  J2 = female pin header, 2 pins [form="♀ (female)"]
  BAT1 = Battery Holders [package=battcon_245mm]

nets:
  N1: Attiny84.(+)_VCC, S1.Pin_3, S1.Pin_4, S2.Pin_3, S2.Pin_4, S3.Pin_3, S3.Pin_4, S4.Pin_3, S4.Pin_4, S5.Pin_3, S5.Pin_4, S6.leg1, S7.Pin_3, S7.Pin_4, J2.pin2
  N2: Attiny84.10, J1.pin1
  N3: Attiny84.9, J1.pin2
  N4: Attiny84.Reset, J1.pin3
  N5: Attiny84.8_PWM, J1.pin4
  N6: Attiny84.7_PWM_AN, R7.Pin_0
  N7: Attiny84.6_PWM_AN_MOSI, R6.Pin_0
  N8: Attiny84.5_AN_PWM_MISO, S5.Pin_1, S5.Pin_2, R5.Pin_1
  N9: Attiny84.4_AN_SCK, S4.Pin_1, S4.Pin_2, R4.Pin_1
  N10: Attiny84.3_AN, S3.Pin_1, S3.Pin_2, R3.Pin_1
  N11: Attiny84.2_AN, S2.Pin_1, S2.Pin_2, R2.Pin_1
  N12: Attiny84.1_AN, S1.Pin_1, S1.Pin_2, R1.Pin_1
  N13: Attiny84.0_AN_AREF, S7.Pin_1, S7.Pin_2, R8.Pin_1
  N14: Attiny84.GND_(-), LED1.anode, LED2.anode, R3.Pin_0, R4.Pin_0, R5.Pin_0, R2.Pin_0, R1.Pin_0, R8.Pin_0, J2.pin1, BAT1.-
  N15: LED1.cathode, R6.Pin_1
  N16: LED2.cathode, R7.Pin_1
  N17: S6.leg0, BAT1.+

notes:
  By Andrew
  Mulholland
  +
  -

custom parts:
  ATTiny84: An Attiny84 DIP chip
