# Fritzing sketch Raspi-Robotic-arm-driver-board (saved by Fritzing 0.8.7b)
circuit board: 8.5cm x 5cm
breadboards: 2

parts:
  IC1 = L293D [package=THT]
  IC2 = L293D [package=THT]
  IC3 = L293D [package=THT]
  Power_plug1 = Power plug
  J1 = Screw terminal - 2 pins [package=THT]
  J2 = Screw terminal - 2 pins [package=THT]
  J3 = Screw terminal - 2 pins [package=THT]
  J4 = Screw terminal - 2 pins [package=THT]
  J5 = Screw terminal - 2 pins [package=THT]
  J7 = female pin header, 2 pins [form="♀ (female)"]
  J8 = female pin header, 2 pins [form="♀ (female)"]
  J9 = female pin header, 2 pins [form="♀ (female)"]
  J10 = female pin header, 2 pins [form="♀ (female)"]
  J11 = female pin header, 2 pins [form="♀ (female)"]
  J12 = female pin header, 2 pins [form="♀ (female)"]
  J6 = Screw terminal - 2 pins [package=THT]
  J13 = female pin header, 6 pins [form="♀ (female)"]
  J14 = female pin header, 2 pins [form="♀ (female)"]
  J15 = Screw terminal - 2 pins [package=THT]
  J16 = female pin header, 6 pins [form="♀ (female)"]
  J17 = female pin header, 2 pins [form="♀ (female)"]
  R1 = Resistor [tolerance=±5% resistance=220 package=THT]
  LED1 = LED - 5mm [color="Red (633nm)" package="5 mm [THT]"]

nets:
  N1: IC1.Enable_1, IC1.+Vmotor, IC1.Enable_2, IC1.+V, IC2.Enable_1, IC2.+Vmotor, IC2.Enable_2, IC2.+V, IC3.Enable_1, IC3.+Vmotor, IC3.Enable_2, IC3.+V, Power_plug1.VCC, J14.pin1, J15.pin1, R1.Pin_0
  N2: IC1.In_1, J13.pin3
  N3: IC1.Out_1_(_Controlled_by_Enable_1_), J3.pin1, J9.pin1
  N4: IC1.0V, IC2.0V, IC3.0V, Power_plug1.GND, J14.pin2, J15.pin2, J17.pin1, J17.pin2, LED1.cathode
  N5: IC1.Out_2_(_Controlled_by_Enable_1_), J3.pin2, J9.pin2
  N6: IC1.In_2, J13.pin4
  N7: IC1.In_3, J16.pin3
  N8: IC1.Out_3_(_Controlled_by_Enable_2_), J10.pin2, J6.pin2
  N9: IC1.Out_4_(_Controlled_by_Enable_2_), J10.pin1, J6.pin1
  N10: IC1.In_4, J16.pin4
  N11: IC2.In_1, J13.pin2
  N12: IC2.Out_1_(_Controlled_by_Enable_1_), J2.pin1, J8.pin1
  N13: IC2.Out_2_(_Controlled_by_Enable_1_), J2.pin2, J8.pin2
  N14: IC2.In_2, J13.pin1
  N15: IC2.In_3, J16.pin6
  N16: IC2.Out_3_(_Controlled_by_Enable_2_), J5.pin2, J11.pin2
  N17: IC2.Out_4_(_Controlled_by_Enable_2_), J5.pin1, J11.pin1
  N18: IC2.In_4, J16.pin5
  N19: IC3.In_1, J13.pin6
  N20: IC3.Out_1_(_Controlled_by_Enable_1_), J1.pin1, J7.pin1
  N21: IC3.Out_2_(_Controlled_by_Enable_1_), J1.pin2, J7.pin2
  N22: IC3.In_2, J13.pin5
  N23: IC3.In_3, J16.pin1
  N24: IC3.Out_3_(_Controlled_by_Enable_2_), J4.pin2, J12.pin2
  N25: IC3.Out_4_(_Controlled_by_Enable_2_), J4.pin1, J12.pin1
  N26: IC3.In_4, J16.pin2
  N27: R1.Pin_1, LED1.anode

notes:
  6 Motor Driver
  By Andrew Mulholland
  -
  +
  GND
